# Fritzing sketch basicLED (saved by Fritzing 0.9.1b)
breadboards: 1

parts:
  Part1 = Arduino Uno (Rev3)
  LED1 = smd LED [color="Red (633nm)" package="1206 [SMD]"]
  R1 = Resistor [package="2010 [SMD]"]

nets:
  N1: Part1.D13/SCK, LED1.cathode
  N2: LED1.anode, R1.Pin_0

notes:
  green -
  yellow +
