# Fritzing sketch LDR_AnalogSensor (saved by Fritzing 0.9.1b)
breadboards: 1

parts:
  Part1 = Arduino Uno (Rev3)
  R1 = Photocell (LDR) [package=THT]
  R2 = Resistor [package="2512 [SMD]"]

nets:
  N1: Part1.A0, R1.pin_1, R2.Pin_0
  N2: Part1.GND, R2.Pin_1
  N3: Part1.3V3, R1.pin_0
