# Fritzing sketch capSensor_Tones (saved by Fritzing 0.9.1b)
breadboards: 1

parts:
  LED1 = LED - 5mm [color="Red (633nm)" package="5 mm [THT]"]
  Part1 = Arduino Uno (Rev3)
  R1 = Resistor [tolerance=±5% resistance=220 package=THT]
  R2 = Resistor [tolerance=±5% resistance=1M package=THT]
  J1 = Piezo Speaker

nets:
  N1: LED1.cathode, R1.Pin_0
  N2: LED1.anode, Part1.D12/MISO
  N3: Part1.D8, J1.pin2
  N4: Part1.GND, R1.Pin_1, J1.pin1
  N5: Part1.D2, R2.Pin_1
  N6: Part1.D4, R2.Pin_0

notes:
  FOIL
